# Fritzing sketch konashiMotorDriveShield (saved by Fritzing 0.7.12b)
perfboards: 1

parts:
  J1 = female pin header, 10 pins [form="♀ (female)"]
  J2 = female pin header, 10 pins [form="♀ (female)"]
  U1 = TA7291P [package=HSIP10-P-2.54(THT)]
  U2 = TA7291P [package=HSIP10-P-2.54(THT)]
  R2 = Resistor [tolerance=±5% resistance=10k package=THT]
  R1 = Resistor [tolerance=±5% resistance=10k power=0pW package=THT]

nets:
  N1: J1.pin4, U2.GND
  N2: J1.pin5, U1.IN2
  N3: J1.pin6, U1.IN1
  N4: J1.pin10, U1.GND
  N5: J2.pin8, U2.IN2
  N6: J2.pin9, U2.IN1
  N7: U1.Vref, R1.Pin_0
  VCC: U1.Vcc, U1.Vs, U2.Vcc, U2.Vs, R2.Pin_1, R1.Pin_1
  N8: U2.Vref, R2.Pin_0

custom parts:
  TA7291P: The IC are Full-Bridge Driver. 4 modes available (CW / CCW / STOP / BRAKE) and PWM control. Output current:1.0 A (AVE.) 2.0 A (PEAK)
